# Fritzing sketch LedStrip (saved by Fritzing 1.0.5)
circuit board: 6.38557cm x 3.59987cm
breadboards: 1

parts:
  Out- = male pin header, 1 pin [form="♂ (male)"]
  Out+ = male pin header, 1 pin [form="♂ (male)"]
  In+ = male pin header, 1 pin [form="♂ (male)"]
  In- = male pin header, 1 pin [form="♂ (male)"]
  MCP1700 = Voltage Regulator [package=to-92]
  1uF = Ceramic Capacitor [capacitance=1µF voltage=35V package="200 mil [THT, multilayer]"]
  1uF_2 = Ceramic Capacitor [capacitance=1µF voltage=35V package="200 mil [THT, multilayer]"]
  NRF24LO1 = NRF24L01+ Breakout Board
  100k = Resistor [tolerance=±5% power=0.25 resistance=100k package=THT]
  R4 = Resistor [tolerance=±5% power=0.25 resistance=470k package=THT]
  Attiny84 = IC, DIP package, 14 pins [chip_label=ATtiny84]
  Bat = male pin header, 2 pins [form="♂ (male)"]
  LED1 = female pin header, 3 pins [form="♀ (female)"]
  switch = female pin header, 3 pins [form="♀ (female)"]
  LED2 = female pin header, 3 pins [form="♀ (female)"]

nets:
  GND: Out-.pin1, In-.pin1, MCP1700.GND, 1uF.0, 1uF_2.0, NRF24LO1.GND, 100k.Pin_1, Attiny84.pin14, Bat.pin2, LED1.pin2, LED2.pin2
  N1: Out+.pin1, LED1.pin1, LED2.pin1
  N2: In+.pin1, R4.Pin_0, Attiny84.pin1, switch.pin3
  N3: MCP1700.IN, 1uF_2.1
  N4: MCP1700.OUT, 1uF.1, NRF24LO1.VCC
  N5: NRF24LO1.CE, Attiny84.pin3
  N6: NRF24LO1.CS, Attiny84.pin5
  N7: NRF24LO1.SCK, Attiny84.pin9
  N8: NRF24LO1.MOSI, Attiny84.pin8
  N9: NRF24LO1.MISO, Attiny84.pin7
  N10: 100k.Pin_0, R4.Pin_1, Attiny84.pin13
  N11: Bat.pin1, switch.pin2

notes:
  VCC
  MT3608
  LED STRIP V1.0
  Battery Light, 1.0
